# Fritzing sketch Schemat elektryczny (saved by Fritzing 0.9.3b)
breadboards: 1

parts:
  Part2 = Arduino Uno (Rev3)
  C1 = Ceramic Capacitor [capacitance=100nF package="100 mil [THT, multilayer]"]
  C2 = Ceramic Capacitor [capacitance=100nF package="100 mil [THT, multilayer]"]
  Part3 = Bluetooth HC-05 Macho
  U1 = SWITCH_SPDT [package=kps-1290]
  U2 = SWITCH_SPDT [package=kps-1290]
  S1 = SPST Switch [package=r_sw_th]
  VCC1 = Battery

nets:
  N1: Part2.A1, U2.S
  N2: Part2.A2, U1.S
  N3: Part2.D8, Part2.D9_PWM, Part2.D11_PWM/MOSI, Part2.D12/MISO
  N4: Part2.D10_PWM/SS, Part3.TXD
  N5: Part2.D13/SCK, Part3.RXD
  N6: Part2.D2, Part2.D4, Part2.D6_PWM, Part2.D7
  N7: Part2.3V3, Part3.Key
  N8: C1.1, C2.0, S1.O
  N9: C2.1, VCC1.+
  N10: S1.P, VCC1.-

notes:
  Zasilanie 7,4V
  Linia zasilanie 6V
  Przetwornica step-down 6V 15A - Pololu - D24V150F6
  Sterownik TB9051FTG
  Zasilanie 5V
  Moduł Bluetooth HC-05
  Moduł GPS L76X
  Krańcówki
